// Logisim project MUX-examples.circ as structural Verilog: 3 circuits, main circuit Mux-4way-1bit
module Mux_4way_1bit (
  input  in_1,
  input  in_2,
  input  in_3,
  input  in_4,
  input  in_5,
  input  in_6,
  output One_Output
);

  wire and_1_out, and_2_out, and_3_out, and_4_out, not_1_out, not_2_out, not_3_out, not_4_out;

  not not_1 (not_1_out, in_5);
  not not_2 (not_2_out, in_6);
  not not_3 (not_3_out, in_5);
  not not_4 (not_4_out, in_6);
  and and_1 (and_1_out, in_1, not_1_out, not_2_out);
  and and_2 (and_2_out, in_2, not_3_out, in_6);
  and and_3 (and_3_out, in_3, in_5, not_4_out);
  and and_4 (and_4_out, in_4, in_5, in_6);
  or or_1 (One_Output, and_1_out, and_2_out, and_3_out, and_4_out);

  // Notes on the sheet:
  //   Four Inputs
  //   Select Wires
  //   Multiplexer
  //   Values on Select Wires
  //   determine which input gets
  //   through to the output
endmodule

module Mux_4way_4bit (
  input  [3:0] in_1,
  input  [3:0] in_2,
  input  [3:0] in_3,
  input  [3:0] in_4,
  input  in_5,
  input  in_6,
  output [3:0] out_7
);

  wire not_1_out, not_2_out, not_3_out, not_4_out;
  wire [3:0] n4_bit_2_control_switch_1_out_4, n4_bit_2_control_switch_2_out_4,
       n4_bit_2_control_switch_3_out_4, n4_bit_2_control_switch_4_out_4;

  not not_1 (not_1_out, in_5);
  not not_2 (not_2_out, in_6);
  not not_3 (not_3_out, in_5);
  not not_4 (not_4_out, in_6);
  _4_bit_2_control_switch u_4_bit_2_control_switch_1 (
    .in_1(in_1), .in_2(not_1_out), .in_3(not_2_out), .out_4(n4_bit_2_control_switch_1_out_4));
  _4_bit_2_control_switch u_4_bit_2_control_switch_2 (
    .in_1(in_2), .in_2(not_3_out), .in_3(in_6), .out_4(n4_bit_2_control_switch_2_out_4));
  _4_bit_2_control_switch u_4_bit_2_control_switch_3 (
    .in_1(in_3), .in_2(in_5), .in_3(not_4_out), .out_4(n4_bit_2_control_switch_3_out_4));
  _4_bit_2_control_switch u_4_bit_2_control_switch_4 (
    .in_1(in_4), .in_2(in_5), .in_3(in_6), .out_4(n4_bit_2_control_switch_4_out_4));
  assign out_7 = n4_bit_2_control_switch_1_out_4 | n4_bit_2_control_switch_2_out_4 | n4_bit_2_control_switch_3_out_4 | n4_bit_2_control_switch_4_out_4;  // OR_Gate or_1, 4 bits wide

  // Notes on the sheet:
  //   Multiplexer with 4-bit inputs and output
endmodule

module _4_bit_2_control_switch (
  input  [3:0] in_1,
  input  in_2,
  input  in_3,
  output [3:0] out_4
);

  wire and_1_out;

  and and_1 (and_1_out, in_2, in_3);
  and and_2 (out_4[0], in_1[0], and_1_out);
  and and_3 (out_4[1], in_1[1], and_1_out);
  and and_4 (out_4[2], in_1[2], and_1_out);
  and and_5 (out_4[3], in_1[3], and_1_out);

  // Notes on the sheet:
  //   This is used in building the Mux-4way-4bit
  //   to replace the AND gate used in the 1-bit version
endmodule
