// Logisim project division.circ as structural Verilog: 1 circuit, main circuit main
module main (
  input  [15:0] DIVIDEND__X,
  input  [15:0] DIVISOR__Y,
  output [15:0] REMAINDER,
  output [15:0] QUOTIENT
);

  wire subtractor_1_bout, subtractor_2_bout, subtractor_3_bout, subtractor_4_bout, subtractor_5_bout,
       subtractor_6_bout, subtractor_7_bout, subtractor_8_bout, subtractor_9_bout, subtractor_10_bout,
       subtractor_11_bout, subtractor_12_bout, subtractor_13_bout, subtractor_14_bout, subtractor_15_bout,
       subtractor_16_bout;
  wire [15:0] adder_1_out, adder_2_out, adder_3_out, adder_4_out, adder_5_out, adder_6_out, adder_7_out,
       adder_8_out, adder_9_out, adder_10_out, adder_11_out, adder_12_out, adder_13_out, adder_14_out,
       adder_15_out, bit_extender_3_out, multiplexer_2_out, multiplexer_4_out, multiplexer_6_out,
       multiplexer_8_out, multiplexer_10_out, multiplexer_12_out, multiplexer_14_out, multiplexer_16_out,
       multiplexer_18_out, multiplexer_20_out, multiplexer_22_out, multiplexer_24_out, multiplexer_26_out,
       multiplexer_28_out, multiplexer_30_out, multiplexer_32_out, shifter_1_out, shifter_3_out,
       shifter_5_out, shifter_7_out, shifter_9_out, shifter_11_out, shifter_13_out, shifter_15_out,
       shifter_17_out, shifter_19_out, shifter_21_out, shifter_23_out, shifter_25_out, shifter_27_out,
       shifter_29_out;
  wire [31:0] bit_extender_1_out, bit_extender_2_out, multiplexer_1_out, multiplexer_3_out,
       multiplexer_5_out, multiplexer_7_out, multiplexer_9_out, multiplexer_11_out, multiplexer_13_out,
       multiplexer_15_out, multiplexer_17_out, multiplexer_19_out, multiplexer_21_out, multiplexer_23_out,
       multiplexer_25_out, multiplexer_27_out, multiplexer_29_out, shifter_2_out, shifter_4_out,
       shifter_6_out, shifter_8_out, shifter_10_out, shifter_12_out, shifter_14_out, shifter_16_out,
       shifter_18_out, shifter_20_out, shifter_22_out, shifter_24_out, shifter_26_out, shifter_28_out,
       shifter_30_out, subtractor_1_out, subtractor_2_out, subtractor_3_out, subtractor_4_out,
       subtractor_5_out, subtractor_6_out, subtractor_7_out, subtractor_8_out, subtractor_9_out,
       subtractor_10_out, subtractor_11_out, subtractor_12_out, subtractor_13_out, subtractor_14_out,
       subtractor_15_out, subtractor_16_out;
  wire [31:16] multiplexer_31_out;

  Multiplexer #(.width(32), .enable("false")) multiplexer_1 (
    .in0(subtractor_1_out), .in1(bit_extender_1_out), .out(multiplexer_1_out), .sel(subtractor_1_bout));
  Multiplexer #(.width(16), .enable("false")) multiplexer_2 (
    .in0(shifter_1_out), .in1({16{1'b0}}), .out(multiplexer_2_out), .sel(subtractor_1_bout));
  Shifter #(.width(16)) shifter_1 (.in(shifter_3_out), .\dist (4'b0001), .out(shifter_1_out));
  Shifter #(.width(32)) shifter_2 (.in(shifter_4_out), .\dist (5'b00001), .out(shifter_2_out));
  Subtractor #(.width(32)) subtractor_1 (
    .a(bit_extender_1_out), .b(shifter_2_out), .out(subtractor_1_out), .bout(subtractor_1_bout));  // open: bin
  Adder #(.width(16)) adder_1 (.a(multiplexer_2_out), .b({16{1'b0}}), .out(adder_1_out));  // open: cin, cout
  Subtractor #(.width(32)) subtractor_2 (
    .a(multiplexer_1_out), .b(shifter_4_out), .out(subtractor_2_out), .bout(subtractor_2_bout));  // open: bin
  Multiplexer #(.width(32), .enable("false")) multiplexer_3 (
    .in0(subtractor_2_out), .in1(multiplexer_1_out), .out(multiplexer_3_out), .sel(subtractor_2_bout));
  Multiplexer #(.width(16), .enable("false")) multiplexer_4 (
    .in0(shifter_3_out), .in1({16{1'b0}}), .out(multiplexer_4_out), .sel(subtractor_2_bout));
  Adder #(.width(16)) adder_2 (.a(multiplexer_4_out), .b(adder_1_out), .out(adder_2_out));  // open: cin, cout
  Shifter #(.width(16)) shifter_3 (.in(shifter_5_out), .\dist (4'b0001), .out(shifter_3_out));
  Shifter #(.width(32)) shifter_4 (.in(shifter_6_out), .\dist (5'b00001), .out(shifter_4_out));
  Multiplexer #(.width(32), .enable("false")) multiplexer_5 (
    .in0(subtractor_3_out), .in1(multiplexer_3_out), .out(multiplexer_5_out), .sel(subtractor_3_bout));
  Multiplexer #(.width(16), .enable("false")) multiplexer_6 (
    .in0(shifter_5_out), .in1({16{1'b0}}), .out(multiplexer_6_out), .sel(subtractor_3_bout));
  Shifter #(.width(16)) shifter_5 (.in(shifter_7_out), .\dist (4'b0001), .out(shifter_5_out));
  Shifter #(.width(32)) shifter_6 (.in(shifter_8_out), .\dist (5'b00001), .out(shifter_6_out));
  Subtractor #(.width(32)) subtractor_3 (
    .a(multiplexer_3_out), .b(shifter_6_out), .out(subtractor_3_out), .bout(subtractor_3_bout));  // open: bin
  Adder #(.width(16)) adder_3 (.a(multiplexer_6_out), .b(adder_2_out), .out(adder_3_out));  // open: cin, cout
  Subtractor #(.width(32)) subtractor_4 (
    .a(multiplexer_5_out), .b(shifter_8_out), .out(subtractor_4_out), .bout(subtractor_4_bout));  // open: bin
  Multiplexer #(.width(32), .enable("false")) multiplexer_7 (
    .in0(subtractor_4_out), .in1(multiplexer_5_out), .out(multiplexer_7_out), .sel(subtractor_4_bout));
  Multiplexer #(.width(16), .enable("false")) multiplexer_8 (
    .in0(shifter_7_out), .in1({16{1'b0}}), .out(multiplexer_8_out), .sel(subtractor_4_bout));
  Adder #(.width(16)) adder_4 (.a(multiplexer_8_out), .b(adder_3_out), .out(adder_4_out));  // open: cin, cout
  Shifter #(.width(16)) shifter_7 (.in(shifter_9_out), .\dist (4'b0001), .out(shifter_7_out));
  Shifter #(.width(32)) shifter_8 (.in(shifter_10_out), .\dist (5'b00001), .out(shifter_8_out));
  Multiplexer #(.width(32), .enable("false")) multiplexer_9 (
    .in0(subtractor_5_out), .in1(multiplexer_7_out), .out(multiplexer_9_out), .sel(subtractor_5_bout));
  Multiplexer #(.width(16), .enable("false")) multiplexer_10 (
    .in0(shifter_9_out), .in1({16{1'b0}}), .out(multiplexer_10_out), .sel(subtractor_5_bout));
  Shifter #(.width(16)) shifter_9 (.in(shifter_11_out), .\dist (4'b0001), .out(shifter_9_out));
  Shifter #(.width(32)) shifter_10 (.in(shifter_12_out), .\dist (5'b00001), .out(shifter_10_out));
  Subtractor #(.width(32)) subtractor_5 (
    .a(multiplexer_7_out), .b(shifter_10_out), .out(subtractor_5_out), .bout(subtractor_5_bout));  // open: bin
  Adder #(.width(16)) adder_5 (.a(multiplexer_10_out), .b(adder_4_out), .out(adder_5_out));  // open: cin, cout
  Subtractor #(.width(32)) subtractor_6 (
    .a(multiplexer_9_out), .b(shifter_12_out), .out(subtractor_6_out), .bout(subtractor_6_bout));  // open: bin
  Multiplexer #(.width(32), .enable("false")) multiplexer_11 (
    .in0(subtractor_6_out), .in1(multiplexer_9_out), .out(multiplexer_11_out), .sel(subtractor_6_bout));
  Multiplexer #(.width(16), .enable("false")) multiplexer_12 (
    .in0(shifter_11_out), .in1({16{1'b0}}), .out(multiplexer_12_out), .sel(subtractor_6_bout));
  Adder #(.width(16)) adder_6 (.a(multiplexer_12_out), .b(adder_5_out), .out(adder_6_out));  // open: cin, cout
  Shifter #(.width(16)) shifter_11 (.in(shifter_13_out), .\dist (4'b0001), .out(shifter_11_out));
  Shifter #(.width(32)) shifter_12 (.in(shifter_14_out), .\dist (5'b00001), .out(shifter_12_out));
  Multiplexer #(.width(32), .enable("false")) multiplexer_13 (
    .in0(subtractor_7_out), .in1(multiplexer_11_out), .out(multiplexer_13_out), .sel(subtractor_7_bout));
  Multiplexer #(.width(16), .enable("false")) multiplexer_14 (
    .in0(shifter_13_out), .in1({16{1'b0}}), .out(multiplexer_14_out), .sel(subtractor_7_bout));
  Shifter #(.width(16)) shifter_13 (.in(shifter_15_out), .\dist (4'b0001), .out(shifter_13_out));
  Shifter #(.width(32)) shifter_14 (.in(shifter_16_out), .\dist (5'b00001), .out(shifter_14_out));
  Subtractor #(.width(32)) subtractor_7 (
    .a(multiplexer_11_out), .b(shifter_14_out), .out(subtractor_7_out), .bout(subtractor_7_bout));  // open: bin
  Adder #(.width(16)) adder_7 (.a(multiplexer_14_out), .b(adder_6_out), .out(adder_7_out));  // open: cin, cout
  Subtractor #(.width(32)) subtractor_8 (
    .a(multiplexer_13_out), .b(shifter_16_out), .out(subtractor_8_out), .bout(subtractor_8_bout));  // open: bin
  Multiplexer #(.width(32), .enable("false")) multiplexer_15 (
    .in0(subtractor_8_out), .in1(multiplexer_13_out), .out(multiplexer_15_out), .sel(subtractor_8_bout));
  Multiplexer #(.width(16), .enable("false")) multiplexer_16 (
    .in0(shifter_15_out), .in1({16{1'b0}}), .out(multiplexer_16_out), .sel(subtractor_8_bout));
  Adder #(.width(16)) adder_8 (.a(multiplexer_16_out), .b(adder_7_out), .out(adder_8_out));  // open: cin, cout
  Shifter #(.width(16)) shifter_15 (.in(shifter_17_out), .\dist (4'b0001), .out(shifter_15_out));
  Shifter #(.width(32)) shifter_16 (.in(shifter_18_out), .\dist (5'b00001), .out(shifter_16_out));
  Multiplexer #(.width(32), .enable("false")) multiplexer_17 (
    .in0(subtractor_9_out), .in1(multiplexer_15_out), .out(multiplexer_17_out), .sel(subtractor_9_bout));
  Multiplexer #(.width(16), .enable("false")) multiplexer_18 (
    .in0(shifter_17_out), .in1({16{1'b0}}), .out(multiplexer_18_out), .sel(subtractor_9_bout));
  Shifter #(.width(16)) shifter_17 (.in(shifter_19_out), .\dist (4'b0001), .out(shifter_17_out));
  Shifter #(.width(32)) shifter_18 (.in(shifter_20_out), .\dist (5'b00001), .out(shifter_18_out));
  Subtractor #(.width(32)) subtractor_9 (
    .a(multiplexer_15_out), .b(shifter_18_out), .out(subtractor_9_out), .bout(subtractor_9_bout));  // open: bin
  Adder #(.width(16)) adder_9 (.a(multiplexer_18_out), .b(adder_8_out), .out(adder_9_out));  // open: cin, cout
  Subtractor #(.width(32)) subtractor_10 (
    .a(multiplexer_17_out), .b(shifter_20_out), .out(subtractor_10_out), .bout(subtractor_10_bout));  // open: bin
  Multiplexer #(.width(32), .enable("false")) multiplexer_19 (
    .in0(subtractor_10_out), .in1(multiplexer_17_out), .out(multiplexer_19_out), .sel(subtractor_10_bout));
  Multiplexer #(.width(16), .enable("false")) multiplexer_20 (
    .in0(shifter_19_out), .in1({16{1'b0}}), .out(multiplexer_20_out), .sel(subtractor_10_bout));
  Adder #(.width(16)) adder_10 (.a(multiplexer_20_out), .b(adder_9_out), .out(adder_10_out));  // open: cin, cout
  Shifter #(.width(16)) shifter_19 (.in(shifter_21_out), .\dist (4'b0001), .out(shifter_19_out));
  Shifter #(.width(32)) shifter_20 (.in(shifter_22_out), .\dist (5'b00001), .out(shifter_20_out));
  Multiplexer #(.width(32), .enable("false")) multiplexer_21 (
    .in0(subtractor_11_out), .in1(multiplexer_19_out), .out(multiplexer_21_out), .sel(subtractor_11_bout));
  Multiplexer #(.width(16), .enable("false")) multiplexer_22 (
    .in0(shifter_21_out), .in1({16{1'b0}}), .out(multiplexer_22_out), .sel(subtractor_11_bout));
  Shifter #(.width(16)) shifter_21 (.in(shifter_23_out), .\dist (4'b0001), .out(shifter_21_out));
  assign bit_extender_1_out = {{16{1'b0}}, DIVIDEND__X};  // Bit_Extender bit_extender_1
  Shifter #(.width(32)) shifter_22 (.in(shifter_24_out), .\dist (5'b00001), .out(shifter_22_out));
  Subtractor #(.width(32)) subtractor_11 (
    .a(multiplexer_19_out), .b(shifter_22_out), .out(subtractor_11_out), .bout(subtractor_11_bout));  // open: bin
  Adder #(.width(16)) adder_11 (.a(multiplexer_22_out), .b(adder_10_out), .out(adder_11_out));  // open: cin, cout
  Subtractor #(.width(32)) subtractor_12 (
    .a(multiplexer_21_out), .b(shifter_24_out), .out(subtractor_12_out), .bout(subtractor_12_bout));  // open: bin
  Multiplexer #(.width(32), .enable("false")) multiplexer_23 (
    .in0(subtractor_12_out), .in1(multiplexer_21_out), .out(multiplexer_23_out), .sel(subtractor_12_bout));
  Multiplexer #(.width(16), .enable("false")) multiplexer_24 (
    .in0(shifter_23_out), .in1({16{1'b0}}), .out(multiplexer_24_out), .sel(subtractor_12_bout));
  Adder #(.width(16)) adder_12 (.a(multiplexer_24_out), .b(adder_11_out), .out(adder_12_out));  // open: cin, cout
  Shifter #(.width(16)) shifter_23 (.in(shifter_25_out), .\dist (4'b0001), .out(shifter_23_out));
  Shifter #(.width(32)) shifter_24 (.in(shifter_26_out), .\dist (5'b00001), .out(shifter_24_out));
  Multiplexer #(.width(32), .enable("false")) multiplexer_25 (
    .in0(subtractor_13_out), .in1(multiplexer_23_out), .out(multiplexer_25_out), .sel(subtractor_13_bout));
  Multiplexer #(.width(16), .enable("false")) multiplexer_26 (
    .in0(shifter_25_out), .in1({16{1'b0}}), .out(multiplexer_26_out), .sel(subtractor_13_bout));
  Shifter #(.width(16)) shifter_25 (.in(shifter_27_out), .\dist (4'b0001), .out(shifter_25_out));
  Shifter #(.width(32)) shifter_26 (.in(shifter_28_out), .\dist (5'b00001), .out(shifter_26_out));
  Subtractor #(.width(32)) subtractor_13 (
    .a(multiplexer_23_out), .b(shifter_26_out), .out(subtractor_13_out), .bout(subtractor_13_bout));  // open: bin
  Adder #(.width(16)) adder_13 (.a(multiplexer_26_out), .b(adder_12_out), .out(adder_13_out));  // open: cin, cout
  Subtractor #(.width(32)) subtractor_14 (
    .a(multiplexer_25_out), .b(shifter_28_out), .out(subtractor_14_out), .bout(subtractor_14_bout));  // open: bin
  Multiplexer #(.width(32), .enable("false")) multiplexer_27 (
    .in0(subtractor_14_out), .in1(multiplexer_25_out), .out(multiplexer_27_out), .sel(subtractor_14_bout));
  Multiplexer #(.width(16), .enable("false")) multiplexer_28 (
    .in0(shifter_27_out), .in1({16{1'b0}}), .out(multiplexer_28_out), .sel(subtractor_14_bout));
  Adder #(.width(16)) adder_14 (.a(multiplexer_28_out), .b(adder_13_out), .out(adder_14_out));  // open: cin, cout
  Shifter #(.width(16)) shifter_27 (.in(shifter_29_out), .\dist (4'b0001), .out(shifter_27_out));
  Shifter #(.width(32)) shifter_28 (.in(shifter_30_out), .\dist (5'b00001), .out(shifter_28_out));
  Multiplexer #(.width(32), .enable("false")) multiplexer_29 (
    .in0(subtractor_15_out), .in1(multiplexer_27_out), .out(multiplexer_29_out), .sel(subtractor_15_bout));
  Multiplexer #(.width(16), .enable("false")) multiplexer_30 (
    .in0(shifter_29_out), .in1({16{1'b0}}), .out(multiplexer_30_out), .sel(subtractor_15_bout));
  Shifter #(.width(16)) shifter_29 (.in(bit_extender_3_out), .\dist (4'b0001), .out(shifter_29_out));
  assign bit_extender_2_out = {{16{1'b0}}, DIVISOR__Y};  // Bit_Extender bit_extender_2
  Shifter #(.width(32)) shifter_30 (.in(bit_extender_2_out), .\dist (5'b00001), .out(shifter_30_out));
  Subtractor #(.width(32)) subtractor_15 (
    .a(multiplexer_27_out), .b(shifter_30_out), .out(subtractor_15_out), .bout(subtractor_15_bout));  // open: bin
  Adder #(.width(16)) adder_15 (.a(multiplexer_30_out), .b(adder_14_out), .out(adder_15_out));  // open: cin, cout
  Subtractor #(.width(32)) subtractor_16 (
    .a(multiplexer_29_out), .b(bit_extender_2_out), .out(subtractor_16_out), .bout(subtractor_16_bout));  // open: bin
  Multiplexer #(.width(32), .enable("false")) multiplexer_31 (
    .in0(subtractor_16_out), .in1(multiplexer_29_out), .out({multiplexer_31_out, REMAINDER}),
    .sel(subtractor_16_bout));
  Multiplexer #(.width(16), .enable("false")) multiplexer_32 (
    .in0(bit_extender_3_out), .in1({16{1'b0}}), .out(multiplexer_32_out), .sel(subtractor_16_bout));
  Adder #(.width(16)) adder_16 (.a(multiplexer_32_out), .b(adder_15_out), .out(QUOTIENT));  // open: cin, cout
  assign bit_extender_3_out = {{15{1'b0}}, 1'b1};  // Bit_Extender bit_extender_3

  // Notes on the sheet:
  //   DIVIDING X BY Y
endmodule
