// Logisim project multiplication.circ as structural Verilog: 2 circuits, main circuit main
module main (
  input  [15:0] X,
  input  [15:0] Y,
  output [31:0] out_3
);

  wire [31:0] adder_1_out, adder_2_out, adder_3_out, adder_4_out, adder_5_out, adder_6_out, adder_7_out,
       adder_8_out, adder_9_out, adder_11_out, adder_12_out, adder_13_out, adder_14_out, adder_15_out,
       bit_extender_1_out, multiplexer_1_out, multiplexer_2_out, multiplexer_3_out, multiplexer_4_out,
       multiplexer_5_out, multiplexer_6_out, multiplexer_7_out, multiplexer_8_out, multiplexer_9_out,
       multiplexer_10_out, multiplexer_11_out, multiplexer_12_out, multiplexer_13_out, multiplexer_14_out,
       multiplexer_15_out, multiplexer_16_out, shifter_1_out, shifter_2_out, shifter_3_out, shifter_4_out,
       shifter_5_out, shifter_6_out, shifter_7_out, shifter_8_out, shifter_9_out, shifter_10_out,
       shifter_11_out, shifter_12_out, shifter_13_out, shifter_14_out, shifter_15_out;

  assign bit_extender_1_out = {{16{1'b0}}, Y};  // Bit_Extender bit_extender_1
  Multiplexer #(.width(32), .enable("false")) multiplexer_1 (
    .in0({32{1'b0}}), .in1(bit_extender_1_out), .out(multiplexer_1_out), .sel(X[0]));
  Shifter #(.width(32)) shifter_1 (.in(bit_extender_1_out), .\dist (5'b00001), .out(shifter_1_out));
  Shifter #(.width(32)) shifter_2 (.in(shifter_1_out), .\dist (5'b00001), .out(shifter_2_out));
  Multiplexer #(.width(32), .enable("false")) multiplexer_2 (
    .in0({32{1'b0}}), .in1(shifter_1_out), .out(multiplexer_2_out), .sel(X[1]));
  Multiplexer #(.width(32), .enable("false")) multiplexer_3 (
    .in0({32{1'b0}}), .in1(shifter_2_out), .out(multiplexer_3_out), .sel(X[2]));
  Adder #(.width(32)) adder_1 (.a(multiplexer_2_out), .b(multiplexer_1_out), .out(adder_1_out));  // open: cin, cout
  Shifter #(.width(32)) shifter_3 (.in(shifter_2_out), .\dist (5'b00001), .out(shifter_3_out));
  Multiplexer #(.width(32), .enable("false")) multiplexer_4 (
    .in0({32{1'b0}}), .in1(shifter_3_out), .out(multiplexer_4_out), .sel(X[3]));
  Shifter #(.width(32)) shifter_4 (.in(shifter_3_out), .\dist (5'b00001), .out(shifter_4_out));
  Multiplexer #(.width(32), .enable("false")) multiplexer_5 (
    .in0({32{1'b0}}), .in1(shifter_4_out), .out(multiplexer_5_out), .sel(X[4]));
  Adder #(.width(32)) adder_2 (.a(multiplexer_4_out), .b(multiplexer_3_out), .out(adder_2_out));  // open: cin, cout
  Shifter #(.width(32)) shifter_5 (.in(shifter_4_out), .\dist (5'b00001), .out(shifter_5_out));
  Multiplexer #(.width(32), .enable("false")) multiplexer_6 (
    .in0({32{1'b0}}), .in1(shifter_5_out), .out(multiplexer_6_out), .sel(X[5]));
  Adder #(.width(32)) adder_3 (.a(adder_2_out), .b(adder_1_out), .out(adder_3_out));  // open: cin, cout
  Shifter #(.width(32)) shifter_6 (.in(shifter_5_out), .\dist (5'b00001), .out(shifter_6_out));
  Multiplexer #(.width(32), .enable("false")) multiplexer_7 (
    .in0({32{1'b0}}), .in1(shifter_6_out), .out(multiplexer_7_out), .sel(X[6]));
  Adder #(.width(32)) adder_4 (.a(multiplexer_6_out), .b(multiplexer_5_out), .out(adder_4_out));  // open: cin, cout
  Shifter #(.width(32)) shifter_7 (.in(shifter_6_out), .\dist (5'b00001), .out(shifter_7_out));
  Multiplexer #(.width(32), .enable("false")) multiplexer_8 (
    .in0({32{1'b0}}), .in1(shifter_7_out), .out(multiplexer_8_out), .sel(X[7]));
  Adder #(.width(32)) adder_5 (.a(multiplexer_8_out), .b(multiplexer_7_out), .out(adder_5_out));  // open: cin, cout
  Shifter #(.width(32)) shifter_8 (.in(shifter_7_out), .\dist (5'b00001), .out(shifter_8_out));
  Multiplexer #(.width(32), .enable("false")) multiplexer_9 (
    .in0({32{1'b0}}), .in1(shifter_8_out), .out(multiplexer_9_out), .sel(X[8]));
  Adder #(.width(32)) adder_6 (.a(adder_5_out), .b(adder_4_out), .out(adder_6_out));  // open: cin, cout
  Shifter #(.width(32)) shifter_9 (.in(shifter_10_out), .\dist (5'b00001), .out(shifter_9_out));
  Shifter #(.width(32)) shifter_10 (.in(shifter_8_out), .\dist (5'b00001), .out(shifter_10_out));
  Multiplexer #(.width(32), .enable("false")) multiplexer_10 (
    .in0({32{1'b0}}), .in1(shifter_9_out), .out(multiplexer_10_out), .sel(X[10]));
  Multiplexer #(.width(32), .enable("false")) multiplexer_11 (
    .in0({32{1'b0}}), .in1(shifter_10_out), .out(multiplexer_11_out), .sel(X[9]));
  Adder #(.width(32)) adder_7 (.a(multiplexer_11_out), .b(multiplexer_9_out), .out(adder_7_out));  // open: cin, cout
  Adder #(.width(32)) adder_8 (.a(adder_6_out), .b(adder_3_out), .out(adder_8_out));  // open: cin, cout
  Shifter #(.width(32)) shifter_11 (.in(shifter_9_out), .\dist (5'b00001), .out(shifter_11_out));
  Multiplexer #(.width(32), .enable("false")) multiplexer_12 (
    .in0({32{1'b0}}), .in1(shifter_11_out), .out(multiplexer_12_out), .sel(X[11]));
  Shifter #(.width(32)) shifter_12 (.in(shifter_11_out), .\dist (5'b00001), .out(shifter_12_out));
  Multiplexer #(.width(32), .enable("false")) multiplexer_13 (
    .in0({32{1'b0}}), .in1(shifter_12_out), .out(multiplexer_13_out), .sel(X[12]));
  Adder #(.width(32)) adder_9 (.a(multiplexer_12_out), .b(multiplexer_10_out), .out(adder_9_out));  // open: cin, cout
  Adder #(.width(32)) adder_10 (.a(adder_15_out), .b(adder_8_out), .out(out_3));  // open: cin, cout
  Shifter #(.width(32)) shifter_13 (.in(shifter_12_out), .\dist (5'b00001), .out(shifter_13_out));
  Multiplexer #(.width(32), .enable("false")) multiplexer_14 (
    .in0({32{1'b0}}), .in1(shifter_13_out), .out(multiplexer_14_out), .sel(X[13]));
  Adder #(.width(32)) adder_11 (.a(adder_9_out), .b(adder_7_out), .out(adder_11_out));  // open: cin, cout
  Shifter #(.width(32)) shifter_14 (.in(shifter_13_out), .\dist (5'b00001), .out(shifter_14_out));
  Multiplexer #(.width(32), .enable("false")) multiplexer_15 (
    .in0({32{1'b0}}), .in1(shifter_14_out), .out(multiplexer_15_out), .sel(X[14]));
  Adder #(.width(32)) adder_12 (.a(multiplexer_14_out), .b(multiplexer_13_out), .out(adder_12_out));  // open: cin, cout
  Shifter #(.width(32)) shifter_15 (.in(shifter_14_out), .\dist (5'b00001), .out(shifter_15_out));
  Multiplexer #(.width(32), .enable("false")) multiplexer_16 (
    .in0({32{1'b0}}), .in1(shifter_15_out), .out(multiplexer_16_out), .sel(X[15]));
  Adder #(.width(32)) adder_13 (.a(multiplexer_16_out), .b(multiplexer_15_out), .out(adder_13_out));  // open: cin, cout
  Shifter #(.width(32)) shifter_16 (.in(shifter_15_out), .\dist (5'b00001));  // open: out
  Adder #(.width(32)) adder_14 (.a(adder_13_out), .b(adder_12_out), .out(adder_14_out));  // open: cin, cout
  Adder #(.width(32)) adder_15 (.a(adder_14_out), .b(adder_11_out), .out(adder_15_out));  // open: cin, cout
endmodule

module Signed_Multiplier (
  input  [15:0] in_1,
  input  [15:0] in_2,
  output [31:0] out_3
);

  wire comparator_1_lt, comparator_2_lt, xor_1_out;
  wire [15:0] multiplexer_1_out, multiplexer_2_out, negator_1_out, negator_2_out;
  wire [31:0] main_1_out_3, negator_3_out;

  // Probe on in_1
  // Probe on in_2
  Comparator #(.width(16)) comparator_1 (.a(in_1), .b({16{1'b0}}), .lt(comparator_1_lt));  // open: gt, eq
  Comparator #(.width(16)) comparator_2 (.a(in_2), .b({16{1'b0}}), .lt(comparator_2_lt));  // open: gt, eq
  Negator #(.width(16)) negator_1 (.in(in_1), .out(negator_1_out));
  Negator #(.width(16)) negator_2 (.in(in_2), .out(negator_2_out));
  Multiplexer #(.width(16)) multiplexer_1 (
    .in0(in_1), .in1(negator_1_out), .out(multiplexer_1_out), .sel(comparator_1_lt));  // open: en
  Multiplexer #(.width(16)) multiplexer_2 (
    .in0(in_2), .in1(negator_2_out), .out(multiplexer_2_out), .sel(comparator_2_lt));  // open: en
  xor xor_1 (xor_1_out, comparator_1_lt, comparator_2_lt);
  main main_1 (.X(multiplexer_2_out), .Y(multiplexer_1_out), .out_3(main_1_out_3));
  Negator #(.width(32)) negator_3 (.in(main_1_out_3), .out(negator_3_out));
  Multiplexer #(.width(32)) multiplexer_3 (
    .in0(main_1_out_3), .in1(negator_3_out), .out(out_3), .sel(xor_1_out));  // open: en
  // Probe on out_3
endmodule
