// Logisim project gates-from-transistors.circ as structural Verilog: 1 circuit, main circuit main
module main (
  input  in_1,
  input  in_2,
  input  in_3,
  input  in_4,
  input  in_5,
  input  in_6,
  output out_7,
  output out_8,
  output out_9,
  output out_10
);

  wire transistor_2_out;

  Transistor transistor_1 (.in(1'b1), .out(out_7), .gate(in_1));
  Pull_Resistor pull_resistor_1 (.node(out_7));
  Transistor #(.\type ("n")) transistor_2 (.in(1'b1), .out(transistor_2_out), .gate(in_5));
  Pull_Resistor pull_resistor_2 (.node(out_10));
  Transistor #(.\type ("n")) transistor_3 (.in(transistor_2_out), .out(out_10), .gate(in_3));
  Pull_Resistor #(.pull(1)) pull_resistor_3 (.node(out_8));
  Transistor #(.\type ("n")) transistor_4 (.in(1'b0), .out(out_8), .gate(in_2));
  Transistor #(.\type ("n")) transistor_5 (.in(1'b1), .out(out_9), .gate(in_4));
  Transistor #(.\type ("n")) transistor_6 (.in(1'b1), .out(out_9), .gate(in_6));
  Pull_Resistor pull_resistor_4 (.node(out_9));

  // Notes on the sheet:
  //   AND gate
  //   NOT gate (P-type transistor)
  //   OR GATE
  //   NOT gate (N-type transistor
endmodule
