// Logisim project lab4.circ as structural Verilog: 6 circuits, main circuit XOR
module main (
  input  [7:0] Input_A,
  input  [7:0] Input_B,
  input  [1:0] Select,
  output [7:0] Output
);

  wire [7:0] add_8_1_sum, and_1_out, or_1_out, subtract_8_1_a___b;

  Add_8 add_8_1 (.Input_A(Input_A), .Input_B(Input_B), .Sum(add_8_1_sum), .carry_in(1'b0));  // open: carry_out
  subtract_8 subtract_8_1 (.A(Input_A), .B(Input_B), .A___B(subtract_8_1_a___b));
  assign and_1_out = Input_A & Input_B;  // AND_Gate and_1, 8 bits wide
  Multiplexer #(.select(2), .width(8)) multiplexer_1 (
    .in0(add_8_1_sum), .in1(subtract_8_1_a___b), .in2(and_1_out), .in3(or_1_out), .out(Output), .sel(Select));  // open: en
  assign or_1_out = Input_A | Input_B;  // OR_Gate or_1, 8 bits wide

  // Notes on the sheet:
  //   Control Wire Settings:
  //   00 = Add
  //   01 = Subtract
  //   10 = And
  //   11 = Or
  //   Subtract
  //   Add
  //   AND
  //   OR
endmodule

module XOR (
  input  A,
  input  B,
  output A_XOR_B
);

  wire and_1_out, and_2_out, not_1_out, not_2_out;

  not not_1 (not_1_out, B);
  not not_2 (not_2_out, A);
  and and_1 (and_1_out, A, not_1_out);
  and and_2 (and_2_out, not_2_out, B);
  or or_1 (A_XOR_B, and_1_out, and_2_out);
endmodule

module Add_1 (
  input  A,
  input  B,
  input  carry_in,
  output carry_out,
  output Sum
);

  wire and_1_out, and_2_out, xor_2_out;

  or or_1 (carry_out, and_1_out, and_2_out);
  and and_1 (and_1_out, A, B);
  and and_2 (and_2_out, xor_2_out, carry_in);
  xor xor_1 (Sum, xor_2_out, carry_in);
  xor xor_2 (xor_2_out, A, B);
endmodule

module Add_8 (
  input  [7:0] Input_A,
  input  [7:0] Input_B,
  input  carry_in,
  output carry_out,
  output [7:0] Sum
);

  wire add_1_2_carry_out, add_1_3_carry_out, add_1_4_carry_out, add_1_5_carry_out, add_1_6_carry_out,
       add_1_7_carry_out, add_1_8_carry_out;

  Add_1 add_1_1 (.carry_out(carry_out), .A(Input_A[7]), .B(Input_B[7]), .Sum(Sum[7]), .carry_in(add_1_2_carry_out));
  Add_1 add_1_2 (
    .carry_out(add_1_2_carry_out), .A(Input_A[6]), .B(Input_B[6]), .Sum(Sum[6]), .carry_in(add_1_3_carry_out));
  Add_1 add_1_3 (
    .carry_out(add_1_3_carry_out), .A(Input_A[5]), .B(Input_B[5]), .Sum(Sum[5]), .carry_in(add_1_4_carry_out));
  Add_1 add_1_4 (
    .carry_out(add_1_4_carry_out), .A(Input_A[4]), .B(Input_B[4]), .Sum(Sum[4]), .carry_in(add_1_5_carry_out));
  Add_1 add_1_5 (
    .carry_out(add_1_5_carry_out), .A(Input_A[3]), .B(Input_B[3]), .Sum(Sum[3]), .carry_in(add_1_6_carry_out));
  Add_1 add_1_6 (
    .carry_out(add_1_6_carry_out), .A(Input_A[2]), .B(Input_B[2]), .Sum(Sum[2]), .carry_in(add_1_7_carry_out));
  Add_1 add_1_7 (
    .carry_out(add_1_7_carry_out), .A(Input_A[1]), .B(Input_B[1]), .Sum(Sum[1]), .carry_in(add_1_8_carry_out));
  Add_1 add_1_8 (.carry_out(add_1_8_carry_out), .A(Input_A[0]), .B(Input_B[0]), .Sum(Sum[0]), .carry_in(carry_in));
endmodule

module subtract_8 (
  input  [7:0] A,
  input  [7:0] B,
  output [7:0] A___B
);

  wire [7:0] not_1_out;

  assign not_1_out = ~B;  // NOT_Gate not_1, 8 bits wide
  Add_8 add_8_1 (.Input_A(A), .Input_B(not_1_out), .Sum(A___B), .carry_in(1'b1));  // open: carry_out
endmodule

module Extra_Credit (
  input  [7:0] Input_A,
  input  [7:0] Input_B,
  input  [1:0] Select,
  output [7:0] Output
);

  wire [7:0] add_8_1_sum, and_1_out, multiplexer_1_out, not_1_out, or_1_out;

  Add_8 add_8_1 (
    .Input_A(Input_A), .Input_B(multiplexer_1_out), .Sum(add_8_1_sum), .carry_in(Select[0]));  // open: carry_out
  assign not_1_out = ~Input_B;  // NOT_Gate not_1, 8 bits wide
  Multiplexer #(.width(8)) multiplexer_1 (
    .in0(Input_B), .in1(not_1_out), .out(multiplexer_1_out), .sel(Select[0]));  // open: en
  assign and_1_out = Input_A & Input_B;  // AND_Gate and_1, 8 bits wide
  Multiplexer #(.select(2), .width(8)) multiplexer_2 (
    .in0(add_8_1_sum), .in1(add_8_1_sum), .in2(and_1_out), .in3(or_1_out), .out(Output), .sel(Select));  // open: en
  assign or_1_out = Input_A | Input_B;  // OR_Gate or_1, 8 bits wide

  // Notes on the sheet:
  //   Control Wire Settings:
  //   00 = Add
  //   01 = Subtract
  //   10 = And
  //   11 = Or
  //   Subtract
  //   Add
  //   AND
  //   OR
endmodule
