// Logisim project lab5.circ as structural Verilog: 5 circuits, main circuit main
module main (
  input  [7:0] Data_in,
  input  [1:0] Select,
  input  Clock,
  output [7:0] Data_out
);

  wire [7:0] adder_1_out, multiplexer_1_out;

  Adder adder_1 (.a(8'h1), .b(Data_out), .out(adder_1_out));  // open: cin, cout
  Multiplexer #(.select(2), .width(8)) multiplexer_1 (
    .in0(Data_in), .in1({8{1'b0}}), .in2(adder_1_out), .in3({1'b0, Data_out[7:1]}), .out(multiplexer_1_out),
    .sel(Select));  // open: en
  Register register_1 (.Data_in(multiplexer_1_out), .Clock(Clock), .Data_out(Data_out));
endmodule

module D_latch (
  input  Data_in,
  input  Load,
  output Data_out
);

  wire and_1_out, and_2_out, and_3_out, not_1_out, not_2_out;

  not not_1 (not_1_out, Data_in);
  and and_1 (and_1_out, Data_in, Load);
  and and_2 (and_2_out, not_1_out, Load);
  not not_2 (not_2_out, and_2_out);
  and and_3 (and_3_out, not_2_out, Data_out);
  or or_1 (Data_out, and_1_out, and_3_out);
endmodule

module D_flip_flop (
  input  Data_in,
  input  Clock,
  output Data_out
);

  wire d_latch_1_data_out, not_1_out;

  D_latch d_latch_1 (.Data_in(Data_in), .Load(Clock), .Data_out(d_latch_1_data_out));
  not not_1 (not_1_out, Clock);
  D_latch d_latch_2 (.Data_in(d_latch_1_data_out), .Load(not_1_out), .Data_out(Data_out));
endmodule

module Register (
  input  [7:0] Data_in,
  input  Clock,
  output [7:0] Data_out
);

  D_flip_flop d_flip_flop_1 (.Data_in(Data_in[0]), .Clock(Clock), .Data_out(Data_out[0]));
  D_flip_flop d_flip_flop_2 (.Data_in(Data_in[1]), .Clock(Clock), .Data_out(Data_out[1]));
  D_flip_flop d_flip_flop_3 (.Data_in(Data_in[2]), .Clock(Clock), .Data_out(Data_out[2]));
  D_flip_flop d_flip_flop_4 (.Data_in(Data_in[3]), .Clock(Clock), .Data_out(Data_out[3]));
  D_flip_flop d_flip_flop_5 (.Data_in(Data_in[4]), .Clock(Clock), .Data_out(Data_out[4]));
  D_flip_flop d_flip_flop_6 (.Data_in(Data_in[5]), .Clock(Clock), .Data_out(Data_out[5]));
  D_flip_flop d_flip_flop_7 (.Data_in(Data_in[6]), .Clock(Clock), .Data_out(Data_out[6]));
  D_flip_flop d_flip_flop_8 (.Data_in(Data_in[7]), .Clock(Clock), .Data_out(Data_out[7]));
endmodule

module RAM (
  input  [7:0] data_in,
  input  [1:0] address,
  input  clock,
  output [7:0] data_out
);

  wire and_1_out, and_2_out, and_3_out, and_4_out, decoder_1_out0, decoder_1_out1, decoder_1_out2,
       decoder_1_out3;
  wire [7:0] register_1_data_out, register_2_data_out, register_3_data_out, register_4_data_out;

  Decoder #(.select(2)) decoder_1 (
    .out0(decoder_1_out0), .out1(decoder_1_out1), .out2(decoder_1_out2), .out3(decoder_1_out3), .sel(address));  // open: en
  and and_1 (and_1_out, decoder_1_out0, clock);
  and and_2 (and_2_out, decoder_1_out1, clock);
  and and_3 (and_3_out, decoder_1_out2, clock);
  and and_4 (and_4_out, decoder_1_out3, clock);
  Register register_1 (.Data_in(data_in), .Clock(and_1_out), .Data_out(register_1_data_out));
  Register register_2 (.Data_in(data_in), .Clock(and_2_out), .Data_out(register_2_data_out));
  Register register_3 (.Data_in(data_in), .Clock(and_3_out), .Data_out(register_3_data_out));
  Register register_4 (.Data_in(data_in), .Clock(and_4_out), .Data_out(register_4_data_out));
  Multiplexer #(.select(2), .width(8)) multiplexer_1 (
    .in0(register_1_data_out), .in1(register_2_data_out), .in2(register_3_data_out),
    .in3(register_4_data_out), .out(data_out), .sel(address));  // open: en
endmodule
