// Logisim project lab6.circ as structural Verilog: 4 circuits, main circuit Count to 9
module Count_to_9 (
  input  Pin_to_Zero
);

  wire and_1_out, clock_1_out, comparator_1_lt;
  wire [7:0] adder_1_out, register_1_q;

  Clock clock_1 (.out(clock_1_out));
  Adder adder_1 (.a(register_1_q), .b(8'h1), .out(adder_1_out));  // open: cin, cout
  and and_1 (and_1_out, comparator_1_lt, clock_1_out);
  Register register_1 (.D(adder_1_out), .Q(register_1_q), .clk(and_1_out), .clr(Pin_to_Zero));  // open: en
  Hex_Digit_Display hex_digit_display_1 (.value(register_1_q[3:0]));  // open: dp
  Comparator comparator_1 (.a(register_1_q), .b(8'h9), .lt(comparator_1_lt));  // open: gt, eq
endmodule

module _3N_1 (
  input  [31:0] Initial_Value,
  input  Load,
  output [31:0] Current_Value
);

  wire and_1_out, clock_1_out, comparator_1_eq, not_1_out, or_1_out;
  wire [31:0] adder_1_out, multiplexer_1_out, multiplexer_2_out, multiplier_1_out, shifter_1_out;

  Clock clock_1 (.out(clock_1_out));
  or or_1 (or_1_out, not_1_out, Load);
  Multiplexer #(.width(32)) multiplexer_1 (
    .in0(multiplexer_2_out), .in1(Initial_Value), .out(multiplexer_1_out), .sel(Load));  // open: en
  and and_1 (and_1_out, or_1_out, clock_1_out);
  Register #(.width(32)) register_1 (.D(multiplexer_1_out), .Q(Current_Value), .clk(and_1_out));  // open: en, clr
  not not_1 (not_1_out, comparator_1_eq);
  Comparator #(.width(32)) comparator_1 (.a(Current_Value), .b(32'h1), .eq(comparator_1_eq));  // open: gt, lt
  Multiplier #(.width(32)) multiplier_1 (.a(Current_Value), .b(32'h3), .out(multiplier_1_out));  // open: cin, cout
  Shifter #(.width(32), .shift("lr")) shifter_1 (.in(Current_Value), .\dist (5'b00001), .out(shifter_1_out));
  Adder #(.width(32)) adder_1 (.a(multiplier_1_out), .b(32'h1), .out(adder_1_out));  // open: cin, cout
  Multiplexer #(.width(32)) multiplexer_2 (
    .in0(shifter_1_out), .in1(adder_1_out), .out(multiplexer_2_out), .sel(Current_Value[0]));  // open: en
  // Probe on Current_Value

  // Notes on the sheet:
  //   To use: Place starting value of N in "Initial Value" input, and
  //   turn the "Load" inptu on and off for at least one clock cycle
  //   3N
  //   Is N odd or even?
  //   Is N equal to 1?
  //   N/2
  //   3N+1
  //   Next Value
endmodule

module Multiply (
  input  [15:0] Input_1,
  input  [15:0] Input_2,
  input  Start,
  output [31:0] Product,
  output Done
);

  wire and_1_out, Clock_out, comparator_1_gt;
  wire [3:0] counter_1_q;
  wire [4:4] counter_1_q_2;
  wire [15:0] register_1_q, register_2_q, shifter_1_out;
  wire [31:0] adder_1_out, bit_extender_1_out, multiplexer_1_out, shifter_2_out;

  // Probe on Input_1
  // Probe on Input_2
  Register #(.width(16), .trigger("falling")) register_1 (.D(Input_1), .Q(register_1_q), .clk(Start));  // open: en, clr
  Clock Clock (.out(Clock_out));
  Register #(.width(16), .trigger("falling")) register_2 (.D(Input_2), .Q(register_2_q), .clk(Start));  // open: en, clr
  assign bit_extender_1_out = {{16{1'b0}}, register_1_q};  // Bit_Extender bit_extender_1
  Shifter #(.width(16), .shift("lr")) shifter_1 (.in(register_2_q), .\dist (counter_1_q), .out(shifter_1_out));
  Counter #(.width(5), .max('h1f), .trigger("falling")) counter_1 (
    .Q({counter_1_q_2[4], counter_1_q}), .clk(and_1_out), .clr(Start));  // open: load, D, count, carry
  Shifter #(.width(32)) shifter_2 (
    .in(bit_extender_1_out), .\dist ({counter_1_q_2[4], counter_1_q}), .out(shifter_2_out));
  and and_1 (and_1_out, comparator_1_gt, Clock_out);
  // Probe on shifter_2_out
  // Probe on shifter_1_out
  Multiplexer #(.width(32)) multiplexer_1 (
    .in0({32{1'b0}}), .in1(shifter_2_out), .out(multiplexer_1_out), .sel(shifter_1_out[0]));  // open: en
  // Probe on shifter_1_out[0]
  Comparator #(.width(16), .mode("unsigned")) comparator_1 (
    .a(shifter_1_out), .b({16{1'b0}}), .gt(comparator_1_gt));  // open: eq, lt
  Adder #(.width(32)) adder_1 (.a(Product), .b(multiplexer_1_out), .out(adder_1_out));  // open: cin, cout
  Register #(.width(32), .trigger("falling")) register_3 (
    .D(adder_1_out), .Q(Product), .clk(and_1_out), .clr(Start));  // open: en
  // Probe on Product
  not not_1 (Done, comparator_1_gt);

  // Notes on the sheet:
  //   Turn "Start" on for at least one clock cycle.
  //   When the final answer is in "Product", the "Done" output is on.
  //   To use: Place the two numbers that are to be multipied into Input-1 and Input-2.
endmodule

module Alternative_Multiply (
  input  [15:0] Input_1,
  input  [15:0] Input_2,
  input  Start,
  output [31:0] Product,
  output Done
);

  wire and_1_out, Clock_out, comparator_1_gt, or_1_out;
  wire [15:0] multiplexer_1_out, register_1_q, shifter_1_out;
  wire [31:0] adder_1_out, bit_extender_1_out, multiplexer_2_out, multiplexer_3_out, register_2_q,
       shifter_2_out;

  // Probe on Input_2
  Clock Clock (.out(Clock_out));
  // Probe on Input_1
  or or_1 (or_1_out, comparator_1_gt, Start);
  Shifter #(.width(16), .shift("lr")) shifter_1 (.in(register_1_q), .\dist (4'b0001), .out(shifter_1_out));
  and and_1 (and_1_out, or_1_out, Clock_out);
  Register #(.width(16), .trigger("falling")) register_1 (
    .D(multiplexer_1_out), .Q(register_1_q), .clk(and_1_out));  // open: en, clr
  Multiplexer #(.width(16)) multiplexer_1 (
    .in0(shifter_1_out), .in1(Input_2), .out(multiplexer_1_out), .sel(Start));  // open: en
  Shifter #(.width(32)) shifter_2 (.in(register_2_q), .\dist (5'b00001), .out(shifter_2_out));
  Multiplexer #(.width(32)) multiplexer_2 (
    .in0(shifter_2_out), .in1(bit_extender_1_out), .out(multiplexer_2_out), .sel(Start));  // open: en
  assign bit_extender_1_out = {{16{1'b0}}, Input_1};  // Bit_Extender bit_extender_1
  Register #(.width(32), .trigger("falling")) register_2 (
    .D(multiplexer_2_out), .Q(register_2_q), .clk(and_1_out));  // open: en, clr
  // Probe on register_2_q
  // Probe on register_1_q
  // Probe on register_1_q[0]
  Comparator #(.width(16), .mode("unsigned")) comparator_1 (
    .a(register_1_q), .b({16{1'b0}}), .gt(comparator_1_gt));  // open: eq, lt
  Multiplexer #(.width(32)) multiplexer_3 (
    .in0({32{1'b0}}), .in1(register_2_q), .out(multiplexer_3_out), .sel(register_1_q[0]));  // open: en
  Adder #(.width(32)) adder_1 (.a(Product), .b(multiplexer_3_out), .out(adder_1_out));  // open: cin, cout
  Register #(.width(32), .trigger("falling")) register_3 (
    .D(adder_1_out), .Q(Product), .clk(and_1_out), .clr(Start));  // open: en
  // Probe on Product
  not not_1 (Done, comparator_1_gt);

  // Notes on the sheet:
  //   Turn "Start" on for at least one clock cycle.
  //   When the final answer is in "Product", the "Done" output is on.
  //   To use: Place the two numbers that are to be multipied into Input-1 and Input-2.
endmodule
