// Logisim project ALU.circ as structural Verilog: 1 circuit, main circuit main
module main (
  input  [15:0] Input_1,
  input  [15:0] Input_2,
  input  [2:0] Select,
  output [15:0] Result
);

  wire comparator_1_lt;
  wire [15:0] adder_1_out, bit_extender_1_out, divider_1_out, multiplier_1_out, nor_1_out, shifter_1_out,
       shifter_2_out, subtractor_1_out;

  Adder #(.width(16)) adder_1 (.a(Input_1), .b(Input_2), .out(adder_1_out));  // open: cin, cout
  Subtractor #(.width(16)) subtractor_1 (.a(Input_1), .b(Input_2), .out(subtractor_1_out));  // open: bin, bout
  Multiplier #(.width(16)) multiplier_1 (.a(Input_1), .b(Input_2), .out(multiplier_1_out));  // open: cin, cout
  Divider #(.width(16)) divider_1 (.a(Input_1), .b(Input_2), .out(divider_1_out));  // open: upper, rem
  Multiplexer #(.select(3), .width(16)) multiplexer_1 (
    .in0(adder_1_out), .in1(subtractor_1_out), .in2(multiplier_1_out), .in3(divider_1_out),
    .in4(shifter_1_out), .in5(shifter_2_out), .in6(nor_1_out), .in7(bit_extender_1_out), .out(Result),
    .sel(Select));  // open: en
  Shifter #(.width(16)) shifter_1 (.in(Input_1), .\dist (Input_2[3:0]), .out(shifter_1_out));
  Shifter #(.width(16), .shift("lr")) shifter_2 (.in(Input_1), .\dist (Input_2[3:0]), .out(shifter_2_out));
  assign nor_1_out = ~(Input_1 | Input_2);  // NOR_Gate nor_1, 16 bits wide
  Comparator #(.width(16)) comparator_1 (.a(Input_1), .b(Input_2), .lt(comparator_1_lt));  // open: gt, eq
  assign bit_extender_1_out = {{15{1'b0}}, comparator_1_lt};  // Bit_Extender bit_extender_1
endmodule
