// Logisim project LARC.circ as structural Verilog: 1 circuit, main circuit main
module main (
  input  PC_0,
  input  Stop_Clock,
  input  Clear_RAM
);

  wire and_1_out, clock_1_out, not_1_out, or_1_out, syscall_1_instruction_is_syscall,
       write_memory_1_write_memory, write_register_1_write_register;
  wire [3:0] decode_instruction_1_opcode, decode_instruction_1_ra, decode_instruction_1_rb,
       decode_instruction_1_rc, multiplexer_1_out;
  wire [15:0] adder_1_out, adder_2_out, decode_instruction_1_shifted_limm,
       decode_instruction_1_sign_extended_limm, decode_instruction_1_sign_extended_simm, main_1_data_out_1,
       main_1_data_out_2, main_2_result, ram_1_data, register_1_q, rom_1_data, select_pc_input_1_to_pc,
       select_register_input_1_to_registers;

  Clock clock_1 (.out(clock_1_out));
  Select_PC_input select_pc_input_1 (
    .Current_PC___1(adder_1_out), .Sign_extended__LIMM(decode_instruction_1_sign_extended_limm),
    .From_register_RB(main_1_data_out_1), .From_register_RA(main_1_data_out_2),
    .OPcode(decode_instruction_1_opcode), .To_PC(select_pc_input_1_to_pc));
  Register #(.width(16)) register_1 (
    .D(select_pc_input_1_to_pc), .Q(register_1_q), .clk(and_1_out), .clr(PC_0));  // open: en
  syscall syscall_1 (.Instruction_is_syscall(syscall_1_instruction_is_syscall), .opcode(decode_instruction_1_opcode));
  not not_1 (not_1_out, or_1_out);
  or or_1 (or_1_out, syscall_1_instruction_is_syscall, Stop_Clock);
  ROM #(.addrWidth(16), .dataWidth(16)) rom_1 (.addr(register_1_q), .data(rom_1_data));  // open: sel
  and and_1 (and_1_out, not_1_out, clock_1_out);
  Adder #(.width(16)) adder_1 (.a(register_1_q), .b(16'h1), .out(adder_1_out));  // open: cin, cout
  Decode_Instruction decode_instruction_1 (
    .Instruction(rom_1_data), .Shifted_LIMM(decode_instruction_1_shifted_limm),
    .sign_extended_LIMM(decode_instruction_1_sign_extended_limm),
    .sign_extended_SIMM(decode_instruction_1_sign_extended_simm), .Opcode(decode_instruction_1_opcode),
    .RA(decode_instruction_1_ra), .RB(decode_instruction_1_rb), .RC(decode_instruction_1_rc));
  Select_Register_Input select_register_input_1 (
    .From_ALU_output(main_2_result), .From_RAM_output(ram_1_data), .From_PC(adder_1_out),
    .Shifted_LIMM(decode_instruction_1_shifted_limm),
    .Sign_extended_LIMM(decode_instruction_1_sign_extended_limm), .Opcode(decode_instruction_1_opcode),
    .To_Registers(select_register_input_1_to_registers));
  Multiplexer #(.width(4)) multiplexer_1 (
    .in0(decode_instruction_1_rc), .in1(decode_instruction_1_ra), .out(multiplexer_1_out),
    .sel(decode_instruction_1_opcode[3]));  // open: en
  registers_main main_1 (
    .ADDR_In(decode_instruction_1_ra), .ADDR_out_1(decode_instruction_1_rb), .ADDR_out_2(multiplexer_1_out),
    .Data_In(select_register_input_1_to_registers), .Clock(and_1_out),
    .Write(write_register_1_write_register), .Data_Out_1(main_1_data_out_1), .Data_Out_2(main_1_data_out_2));
  Write_Register write_register_1 (
    .Opcode(decode_instruction_1_opcode), .Write_Register(write_register_1_write_register));
  ALU_main main_2 (
    .Select(decode_instruction_1_opcode[2:0]), .Input_1(main_1_data_out_1), .Input_2(main_1_data_out_2),
    .Result(main_2_result));
  Adder #(.width(16)) adder_2 (
    .a(main_1_data_out_1), .b(decode_instruction_1_sign_extended_simm), .out(adder_2_out));  // open: cin, cout
  Write_Memory write_memory_1 (.opcode(decode_instruction_1_opcode), .Write_Memory(write_memory_1_write_memory));
  RAM #(.addrWidth(16), .dataWidth(16), .bus("separate")) ram_1 (
    .addr(adder_2_out), .din(main_1_data_out_2), .data(ram_1_data), .str(write_memory_1_write_memory),
    .clk(and_1_out), .clr(Clear_RAM));  // open: sel, ld

  // Notes on the sheet:
  //   Select PC input
  //   PC
  //   syscall?
  //   contents of rom_1 (hex, n*v repeats v):
  //   8103 9202 83c9 412 1512 2612 3721 4821 5921 6a12 7b12 8c00 8d11 ddc0 cec0 8f02 def1 deff 8c01 8d03
  //   8e04 ad04 dde0 1ddc eec a0fb bc01 dce0 802a 8d20 ecd0 8c00 8f08 8e01 d0f0 ffe d1f0 ffe d2f0 ffe d3f0
  //   ffe d4f0 ffe d5f0 ffe d6f0 ffe d7f0 ffe d8f0 ffe d9f0 ffe daf0 ffe dbf0 ffe dcf0 ffe ddf0 ffe def0
  //   ffe dff0 8100 f000
  //   Instruction ROM
  //   Decode
  //   instruction
  //   Select Register Input
  //   Write Reg?
  //   Registers
  //   ALU
  //   Write RAM?
  //   Data RAM
endmodule
