// Logisim project util.circ as structural Verilog: 6 circuits, main circuit Select PC input
module Select_PC_input (
  input  [15:0] Current_PC___1,
  input  [15:0] Sign_extended__LIMM,
  input  [15:0] From_register_RB,
  input  [15:0] From_register_RA,
  input  [3:0] OPcode,
  output [15:0] To_PC
);

  wire and_1_out, and_2_out, and_3_out, and_4_out, comparator_1_eq, not_1_out, not_2_out, not_3_out,
       not_4_out, not_5_out;
  wire [1:0] and_5_out;
  wire [15:0] adder_1_out;

  Comparator #(.width(16)) comparator_1 (.a({16{1'b0}}), .b(From_register_RA), .eq(comparator_1_eq));  // open: gt, lt
  not not_1 (not_1_out, OPcode[2]);
  not not_2 (not_2_out, OPcode[0]);
  not not_3 (not_3_out, OPcode[2]);
  and and_1 (and_1_out, OPcode[3], not_1_out, OPcode[1], not_2_out);
  and and_2 (and_2_out, OPcode[3], not_3_out, OPcode[1], OPcode[0]);
  not not_4 (not_4_out, OPcode[0]);
  Adder #(.width(16)) adder_1 (.a(Current_PC___1), .b(Sign_extended__LIMM), .out(adder_1_out));  // open: cin, cout
  and and_3 (and_3_out, comparator_1_eq, and_1_out);
  not not_5 (not_5_out, comparator_1_eq);
  and and_4 (and_4_out, not_5_out, and_2_out);
  and and_5 (and_5_out[0], OPcode[3], OPcode[2], OPcode[1], not_4_out);
  or or_1 (and_5_out[1], and_3_out, and_4_out, and_5_out[0]);
  Multiplexer #(.select(2), .width(16)) multiplexer_1 (
    .in0(Current_PC___1), .in1(Current_PC___1), .in2(adder_1_out), .in3(From_register_RB), .out(To_PC),
    .sel(and_5_out));  // open: en
endmodule

module Decode_Instruction (
  input  [15:0] Instruction,
  output [15:0] Shifted_LIMM,
  output [15:0] sign_extended_LIMM,
  output [15:0] sign_extended_SIMM,
  output [3:0] Opcode,
  output [3:0] RA,
  output [3:0] RB,
  output [3:0] RC
);

  wire [15:0] bit_extender_1_out;

  assign bit_extender_1_out = {{8{1'b0}}, Instruction[7:0]};  // Bit_Extender bit_extender_1
  Shifter #(.width(16)) shifter_1 (.in(bit_extender_1_out), .\dist (4'b1000), .out(Shifted_LIMM));
  assign sign_extended_LIMM = {{8{Instruction[7]}}, Instruction[7:0]};  // Bit_Extender bit_extender_2
  assign sign_extended_SIMM = {{12{Instruction[3]}}, Instruction[3:0]};  // Bit_Extender bit_extender_3

  assign Opcode = Instruction[15:12];
  assign RA = Instruction[11:8];
  assign RB = Instruction[7:4];
  assign RC = Instruction[3:0];
endmodule

module Select_Register_Input (
  input  [15:0] From_ALU_output,
  input  [15:0] From_RAM_output,
  input  [15:0] From_PC,
  input  [15:0] Shifted_LIMM,
  input  [15:0] Sign_extended_LIMM,
  input  [3:0] Opcode,
  output [15:0] To_Registers
);

  wire and_1_out, and_2_out, and_3_out, not_1_out, not_2_out, not_3_out, not_4_out, not_5_out, not_6_out;
  wire [1:0] or_2_out;
  wire [15:0] multiplexer_1_out;

  Multiplexer #(.width(16)) multiplexer_1 (
    .in0(Shifted_LIMM), .in1(Sign_extended_LIMM), .out(multiplexer_1_out), .sel(not_1_out));  // open: en
  not not_1 (not_1_out, Opcode[0]);
  not not_2 (not_2_out, Opcode[2]);
  not not_3 (not_3_out, Opcode[1]);
  not not_4 (not_4_out, Opcode[1]);
  not not_5 (not_5_out, Opcode[0]);
  not not_6 (not_6_out, Opcode[0]);
  and and_1 (and_1_out, Opcode[3], not_2_out, not_3_out);
  and and_2 (and_2_out, Opcode[3], Opcode[2], not_4_out, not_5_out);
  and and_3 (and_3_out, Opcode[3], Opcode[2], Opcode[1], not_6_out);
  or or_1 (or_2_out[1], and_1_out, and_3_out);
  or or_2 (or_2_out[0], and_1_out, and_2_out);
  Multiplexer #(.select(2), .width(16)) multiplexer_2 (
    .in0(From_ALU_output), .in1(From_RAM_output), .in2(From_PC), .in3(multiplexer_1_out), .out(To_Registers),
    .sel(or_2_out));  // open: en

  // Notes on the sheet:
  //   lw
  //   jalr
  //   LIMM instruction
endmodule

module Write_Register (
  input  [3:0] Opcode,
  output Write_Register
);

  wire and_1_out, and_2_out, not_1_out, not_2_out, not_3_out, not_4_out;

  not not_1 (not_1_out, Opcode[3]);
  not not_2 (not_2_out, Opcode[1]);
  not not_3 (not_3_out, Opcode[2]);
  not not_4 (not_4_out, Opcode[0]);
  and and_1 (and_1_out, not_2_out, not_3_out, Opcode[3]);
  and and_2 (and_2_out, not_4_out, Opcode[2], Opcode[3]);
  or or_1 (Write_Register, not_1_out, and_1_out, and_2_out);
endmodule

module Write_Memory (
  input  [3:0] opcode,
  output Write_Memory
);

  wire not_1_out;

  not not_1 (not_1_out, opcode[1]);
  and and_1 (Write_Memory, opcode[0], not_1_out, opcode[2], opcode[3]);
endmodule

module syscall (
  input  [3:0] opcode,
  output Instruction_is_syscall
);

  and and_1 (Instruction_is_syscall, opcode[0], opcode[1], opcode[2], opcode[3]);
endmodule
